# Fritzing sketch coffeeboxcounter (saved by Fritzing 0.9.3b)

parts:
  WeMos_D1_Mini1 = WeMos D1 Mini
  S1 = Round Pushbutton
  J1 = Piezo Speaker
  SG1 = Buzzer 12mm [package=buzzer-cmt1102]  # not connected
  Grove1 = Grove OLED 128x96
  R1 = Resistor [tolerance=±5% resistance=220 package="1206 [SMD]"]

nets:
  3V3: WeMos_D1_Mini1.3V3, Grove1.VCC, R1.Pin_0
  N1: WeMos_D1_Mini1.D0, S1.leg0
  N2: WeMos_D1_Mini1.D1, Grove1.SCL
  N3: WeMos_D1_Mini1.D2, Grove1.SDA
  N4: WeMos_D1_Mini1.D4, J1.pin2
  N5: WeMos_D1_Mini1.G, J1.pin1, Grove1.GND
  N6: S1.leg1, R1.Pin_1
